// Digital circuit Computer.dig as structural Verilog
module Computer (
  input  C
);

  wire addressdecoder_1_a_dev, addressdecoder_1_a_io, addressdecoder_1_a_ram, addressdecoder_1_a_vram,
       addressdecoder_1_a_vramctl, cpu_1_halted, cpu_1_re, cpu_1_we;
  wire [31:0] cpu_1_addressbus, cpu_1_databus_out, gpu_1_d_out;

  CPU cpu_1 (
    .Clock(C), .Databus_in(gpu_1_d_out), .Addressbus(cpu_1_addressbus), .Databus_out(cpu_1_databus_out),
    .RE(cpu_1_re), .WE(cpu_1_we), .Halted(cpu_1_halted));
  AddressDecoder addressdecoder_1 (
    .A(cpu_1_addressbus), .A_ram(addressdecoder_1_a_ram), .A_io(addressdecoder_1_a_io),
    .A_dev(addressdecoder_1_a_dev), .A_vramctl(addressdecoder_1_a_vramctl), .A_vram(addressdecoder_1_a_vram));  // open: A_unknown
  GPU #(.generic("Height := 48; Width := 64;")) gpu_1 (
    .C(C), .RE(cpu_1_re), .WE(cpu_1_we), .D_in(cpu_1_databus_out), .A(cpu_1_addressbus),
    .A_vramctl(addressdecoder_1_a_vramctl), .A_vram(addressdecoder_1_a_vram), .D_out(gpu_1_d_out));
  RAM ram_1 (
    .C(C), .RE(cpu_1_re), .WE(cpu_1_we), .D_in(cpu_1_databus_out), .A(cpu_1_addressbus),
    .A_ram(addressdecoder_1_a_ram), .D_out(gpu_1_d_out));
  DevInfo #(.generic("clockrate := 50000;")) devinfo_1 (
    .C(C), .RE(cpu_1_re), .A(cpu_1_addressbus), .A_dev(addressdecoder_1_a_dev), .D_out(gpu_1_d_out));
  Terminal #(.generic("LineWidth := 80; Lines := 24;")) terminal_1 (
    .C(C), .RE(cpu_1_re), .WE(cpu_1_we), .D_in(cpu_1_databus_out), .A(cpu_1_addressbus),
    .A_io(addressdecoder_1_a_io), .D_out(gpu_1_d_out));
  Break break_1 (.brk(cpu_1_halted));
  Stop stop_1 (.stop(cpu_1_halted));
  // Probe halted on cpu_1_halted
  // Probe RE on cpu_1_re
  // Probe WE on cpu_1_we
  // Probe databusToCPU on gpu_1_d_out
  // Probe databusFromCPU on cpu_1_databus_out
  // Probe addressbus on cpu_1_addressbus
  // Probe address_ram on addressdecoder_1_a_ram
  // Probe address_io on addressdecoder_1_a_io
  // Probe address_dev on addressdecoder_1_a_dev
  // Probe address_vramctl on addressdecoder_1_a_vramctl
  // Probe address_vram on addressdecoder_1_a_vram

  // Notes on the sheet:
  //   C: Hz: 5000
  //   Original Hades design by David N. Jansen, Radboud Universiteit Nijmegen, Nederland (2012)
  //   Ported to Digital and modified by Ciske Harsema (2019+2020)
endmodule
