// Digital circuit AddressDecoder.dig as structural Verilog
// Decodes an address to determine in which address range it belongs.
module AddressDecoder (
  input  [31:0] A,
  output A_ram,
  output A_io,
  output A_dev,
  output A_vramctl,
  output A_vram,
  output A_unknown
);

  wire [31:0] and_1_out, and_2_out, and_3_out, and_4_out, and_5_out;

  assign and_1_out = A & 32'hfffc0000;  // And and_1, 32 bits wide
  assign and_2_out = A & 32'hff000000;  // And and_2, 32 bits wide
  assign and_3_out = A & 32'hfffffff0;  // And and_3, 32 bits wide
  assign and_4_out = A & 32'hfffffff0;  // And and_4, 32 bits wide
  assign and_5_out = A & 32'hfffffff0;  // And and_5, 32 bits wide
  Comparator #(.Bits(32)) comparator_1 (.a(and_1_out), .b({32{1'b0}}), .eq(A_ram));  // open: gt, lt
  Comparator #(.Bits(32)) comparator_2 (.a(and_2_out), .b(32'h1000000), .eq(A_vram));  // open: gt, lt
  Comparator #(.Bits(32)) comparator_3 (.a(and_3_out), .b(32'hfffffe00), .eq(A_io));  // open: gt, lt
  Comparator #(.Bits(32)) comparator_4 (.a(and_4_out), .b(32'hfffffe10), .eq(A_vramctl));  // open: gt, lt
  Comparator #(.Bits(32)) comparator_5 (.a(and_5_out), .b(32'hfffffe20), .eq(A_dev));  // open: gt, lt
  nor nor_1 (A_unknown, A_dev, A_vramctl, A_io, A_vram, A_ram);

  // Notes on the sheet:
  //   A: The address to decode.
  //   A_ram: Indicates wheter the address decoded to the RAM address range.
  //   A_io: Indicates wheter the address decoded to the IO address range.
  //   A_dev: Indicates wheter the address decoded to the device information address range.
  //   A_vramctl: Indicates wheter the address decoded to the VRAM control address range.
  //   A_vram: Indicates wheter the address decoded to the VRAM address range.
  //   A_unknown: Indicates wheter the address did not decode to any known address range.
endmodule
