// Digital circuit ALU.dig as structural Verilog
// The Arithmetic Logic Unit (ALU) component, which can perform various operations on the provided operands, also determining the resulting flag values.
module ALU (
  input  [2:0] Opcode,
  input  [31:0] B,
  input  [31:0] A,
  output [31:0] Result,
  output Carry,
  output Overflow,
  output Negative,
  output Zero
);

  wire and_2_out, and_3_out, and_4_out, and_5_out, sub_1_c_o;
  wire [31:0] add_1_s, and_1_out, or_1_out, rotateleft_1_p3, shiftleft_1_p3, shiftright_1_p3, sub_1_s,
       xor_1_out;
  wire [32:32] shiftright_1_p4;
  wire [33:32] or_2_out, or_3_out, xor_2_out, xor_3_out;

  assign or_1_out = B | A;  // Or or_1, 32 bits wide
  assign xor_1_out = B ^ A;  // XOr xor_1, 32 bits wide
  assign and_1_out = B & A;  // And and_1, 32 bits wide
  // ShiftLeft shiftleft_1: pin names not known; wires that end beside it: A, B, shiftleft_1_p3, xor_2_out[32]
  // ShiftRight shiftright_1: pin names not known; wires that end beside it: A, B, shiftright_1_p3, shiftright_1_p4[32]
  // RotateLeft rotateleft_1: pin names not known; wires that end beside it: A, B, rotateleft_1_p3, xor_3_out[32]
  Add #(.Bits(32)) add_1 (.a(A), .b(B), .c_i(1'b0), .s(add_1_s), .c_o(or_2_out[32]));
  Sub #(.Bits(32)) sub_1 (.a(A), .b(B), .c_i(1'b0), .s(sub_1_s), .c_o(sub_1_c_o));
  not not_1 (or_3_out[32], sub_1_c_o);
  xor xor_2 (xor_2_out[33], shiftleft_1_p3[31], xor_2_out[32]);
  xor xor_3 (xor_3_out[33], rotateleft_1_p3[31], xor_3_out[32]);
  and and_2 (and_2_out, A[31], ~B[31], ~sub_1_s[31]);  // And
  and and_3 (and_3_out, ~A[31], B[31], sub_1_s[31]);  // And
  and and_4 (and_4_out, B[31], B[31], ~add_1_s[31]);  // And
  and and_5 (and_5_out, ~A[31], ~B[31], add_1_s[31]);  // And
  or or_2 (or_2_out[33], and_4_out, and_5_out);
  or or_3 (or_3_out[33], and_2_out, and_3_out);
  Multiplexer #(.Selector_Bits(3), .Bits(34)) multiplexer_1 (
    .sel(Opcode), .in_0({2'b00, or_1_out}), .in_1({2'b00, xor_1_out}), .in_2({2'b00, and_1_out}),
    .in_3({xor_2_out, shiftleft_1_p3}), .in_4({B[31], shiftright_1_p4[32], shiftright_1_p3}),
    .in_5({xor_3_out, rotateleft_1_p3}), .in_6({or_2_out, add_1_s}), .in_7({or_3_out, sub_1_s}),
    .out({Overflow, Carry, Negative, Result[30:0]}));
  Comparator #(.Bits(32)) comparator_1 (.a({Negative, Result[30:0]}), .b({32{1'b0}}), .eq(Zero));  // open: gt, lt

  assign Result[31] = Negative;

  // Notes on the sheet:
  //   Opcode: The ALU opcode, which specifies the operation to perform.
  //   B: The value of the ALU B operand.
  //   A: The value of the ALU A operand.
  //   Result: The resuling value, containing the value computed by the ALU.
  //   Carry: The resulting carry flag.
  //   Overflow: The resulting overflow flag.
  //   Negative: The resulting negative flag.
  //   Zero: The resulting zero flag.
  //   XOR
  //   AND
  //   SHL
  //   SHR
  //   ROL
  //   ADD
  //   SUB
endmodule

/* Test case Sub:
A B Opcode Result Carry Overflow Negative Zero

loop(i, 256)
    # determine random values for A and B inputs
    let a = random(1<<32);
    let b = random(1<<32);

    # compute expected Result
    let r = a + (~b & 0xffffffff) + 1;

    # determine expected flags
    let c = (r) >= (1<<32);
    let o = (((a>>31)&1) != ((b>>31)&1)) & (((a>>31)&1) != ((r>>31)&1));
    let n = (r>>31) & 1;
    let z = r=0;

    # perform subtraction, and then check Result and flags are as expected
    (a) (b) 7 (r) (c) (o) (n) (z)
end loop
*/

/* Test case Rol:
A B Opcode Result Carry Overflow Negative Zero

loop(i, 256)
    # determine random values for A and B inputs
    let a = random(1<<32);
    let b = random(1<<32);

    # compute expected Result
    let rot = a&31;
    let r = (b << rot) | (b >> (32-rot));

    # determine expected flags
    let c = ite(a = 0, 0, r & 1);
    let o = c != ((r>>31)&1);
    let n = (r>>31) & 1;
    let z = r=0;

    # perform rotation, and then check Result and flags are as expected
    (a) (b) 5 (r) (c) (o) (n) (z)
end loop

loop(i, 16)
    # determine random values for inputs
    # set A to 0 to test edge case for Carry flag
    let a = 0;
    let b = random(1<<32);

    # compute expected Result
    let rot = a&31;
    let r = (b << rot) | (b >> (32-rot));

    # determine expected flags
    let c = ite(a = 0, 0, r & 1);
    let o = c != ((r>>31)&1);
    let n = (r>>31) & 1;
    let z = r=0;

    # perform rotation, and then check Result and flags are as expected
    (a) (b) 5 (r) (c) (o) (n) (z)
end loop
*/

/* Test case Shr:
A B Opcode Result Carry Overflow Negative Zero

loop(i, 256)
    # determine random values for A and B inputs
    let a = random(1<<32) & 0x3f;
    let b = random(1<<32);

    # compute expected Result
    let r = ite((a >= 0 & a <= 32), ((b >> a) & 0xffffffff), 0);

    # determine expected flags
    let c = ite(a = 0 | a > 32, 0, (b >> (a-1)) & 1);
    let o = (b>>31) & 1;
    let n = (r>>31) & 1;
    let z = r=0;

    # perform logical shift right, and then check Result and flags are as expected
    (a) (b) 4 (r) (c) (o) (n) (z)
end loop
*/

/* Test case Shl:
A B Opcode Result Carry Overflow Negative Zero

loop(i, 256)
    # determine random values for A and B inputs
    let a = random(1<<32) & 0x3f;
    let b = random(1<<32);

    # compute expected Result
    let r = ite((a >= 0 & a <= 32), (b << a) & 0xffffffff, 0);

    # determine expected flags
    let c = ite(a = 0 | a > 32, 0, (b >> (32-a)) & 1);
    let o = c != ((r>>31)&1);
    let n = (r>>31) & 1;
    let z = r=0;

    # perform logical shift left, and then check Result and flags are as expected
    (a) (b) 3 (r) (c) (o) (n) (z)
end loop
*/
