// Digital circuit CPU.dig as structural Verilog
// The Radboud University Nijmegen Central Processing Unit (RUNCPU), which is a basic 32-bit CPU for the Processors course, part of the Computing Science Bachelor.
module CPU (
  input  Clock,
  input  [31:0] Databus_in,
  output [31:0] Addressbus,
  output [31:0] Databus_out,
  output RE,
  output WE,
  output Halted
);

  wire ALU_carry, ALU_negative, ALU_overflow, ALU_zero, decoder_1_out_1, decoder_1_out_3, decoder_1_out_5,
       FlagRegisterBank_carry_out, FlagRegisterBank_negative_out, FlagRegisterBank_overflow_out,
       FlagRegisterBank_zero_out, InstructionDecoder_f, not_1_out, Tester_testsucceeds, Timer_execute,
       Timer_fetch;
  wire [2:0] InstructionDecoder_format, InstructionDecoder_opcode;
  wire [3:0] InstructionDecoder_condition, InstructionDecoder_reg_a, InstructionDecoder_reg_b,
       InstructionDecoder_reg_dest;
  wire [31:0] InstructionDecoder_constant, multiplexer_1_out, multiplexer_2_out, RegisterBank_p6;

  Timer Timer (
    .Clock(Clock), .TestSucceeds(Tester_testsucceeds), .Halt(decoder_1_out_1), .Halted(Halted),
    .Fetch(Timer_fetch), .Execute(Timer_execute));
  InstructionDecoder InstructionDecoder (
    .Instruction(Databus_in), .Fetch(Timer_fetch), .Execute(Timer_execute), .Clock(Clock),
    .Reg_dest(InstructionDecoder_reg_dest), .Reg_B(InstructionDecoder_reg_b),
    .Reg_A(InstructionDecoder_reg_a), .Opcode(InstructionDecoder_opcode),
    .Constant(InstructionDecoder_constant), .Format(InstructionDecoder_format), .f(InstructionDecoder_f),
    .Condition(InstructionDecoder_condition));
  Decoder #(.Selector_Bits(3)) decoder_1 (
    .sel(InstructionDecoder_format), .out_1(decoder_1_out_1), .out_2(WE), .out_3(decoder_1_out_3),
    .out_5(decoder_1_out_5));  // open: out_0, out_4, out_6, out_7
  Multiplexer #(.Bits(32)) multiplexer_1 (
    .sel(decoder_1_out_3), .in_0(Addressbus), .in_1(Databus_in), .out(multiplexer_1_out));
  or or_1 (RE, decoder_1_out_3, Timer_fetch);
  // RegisterBank RegisterBank: pin names not known; wires that end beside it: multiplexer_1_out, InstructionDecoder_reg_dest, InstructionDecoder_reg_b, InstructionDecoder_reg_a, Clock, RegisterBank_p6, Databus_out
  FlagRegisterBank FlagRegisterBank (
    .Carry_in(ALU_carry), .Overflow_in(ALU_overflow), .Negative_in(ALU_negative), .Zero_in(ALU_zero),
    .Set(InstructionDecoder_f), .Clock(Clock), .Carry_out(FlagRegisterBank_carry_out),
    .Overflow_out(FlagRegisterBank_overflow_out), .Negative_out(FlagRegisterBank_negative_out),
    .Zero_out(FlagRegisterBank_zero_out));
  Multiplexer #(.Bits(32)) multiplexer_2 (
    .sel(not_1_out), .in_0(Databus_out), .in_1(InstructionDecoder_constant), .out(multiplexer_2_out));
  not not_1 (not_1_out, decoder_1_out_5);
  Tester Tester (
    .Carry(FlagRegisterBank_carry_out), .Overflow(FlagRegisterBank_overflow_out),
    .Negative(FlagRegisterBank_negative_out), .Zero(FlagRegisterBank_zero_out),
    .Condition(InstructionDecoder_condition), .TestSucceeds(Tester_testsucceeds));
  ALU ALU (
    .Opcode(InstructionDecoder_opcode), .B(RegisterBank_p6), .A(multiplexer_2_out), .Result(Addressbus),
    .Carry(ALU_carry), .Overflow(ALU_overflow), .Negative(ALU_negative), .Zero(ALU_zero));

  // Notes on the sheet:
  //   Clock: Hz: 100
  //   Addressbus: The addressbus signal, which determines the address of a read or write operation. For a write operation the address is where a value being written by the CPU should be stored. For a read operation the address is where a value being read by the CPU should be read from.
  //   Databus_out: The databus signal from the CPU. Any values written by the CPU will be stored here.
  //   Databus_in: The databus signal to the CPU. Any values read (or instructions fetched) by the CPU will be stored here.
  //   RE: Read enabled signal. When a read operation is performed by the CPU this value is set to high.
  //   WE: Write enabled signal. When a write operation is performed by the CPU this value is set to high.
  //   Halted: Determines whether the CPU is in the halted state, in which it shall remain until the CPU is restarted.
  //   if READ
  //   HALT
  //   WRITE
  //   READ
  //   ARITH3
  //   else
  //   Fetch OR Read -> RE
  //   if ARITH3
endmodule

/* Test case init:
Clock Databus_in Halted RE WE Databus_out Addressbus
0     0          0      1  0  x           0
*/

/* Test case add:
Clock Databus_in Halted RE WE Databus_out Addressbus R3
# The first line of test data must be the header, which contains the inputs and outputs used in the test case.
# It is possible to use registers in test cases by enabling their 'use as measurement value' attribute in the advanced tab.
# The R0-R15 registers have this attribute enabled in the provided template.

# These init statements are used to set the register contents when the simulation is started.
# Note that all init statements are collected and executed first. Interleaving them with regular test data has no effect.
# If you wish to test other instructions, or with different values, you must add a new test case component to the circuit.
# If you do not do this, the tests will run sequentially, meaning the next test will use the CPU state obtained after executing the prior test.
# This is reflected below in the last test data row that checks if the program counter increased by 4.
init R1=4;
init R2=5;

# ADD R1, R2, R3
# The four test data lines below describe the testing of the ADD R1, R2, R3 instruction.
# We first load the machine code into the Databus_in, and then drive the clock to step through the full instruction cycle once.
# Note that the first two columns (in this case) are inputs, meaning they will be set to the provided value.
# The other columns are outputs, which are evaluated after the inputs have been set, and then compared against the given expected values.
# The value 'x' denotes a 'do not care' value. Please click the 'Help' button in this dialog for more information regarding test cases.
0     0x6400123f 0      1  0  x           0          x
1     0x6400123f 0      x  x  x           x          x
0     0          0      0  0  x           x          x
1     0          0      0  0  x           x          9

# Fetch next instruction, check if the program counter increased by 4...
0     0          0      1  0  x           4          x
*/
