// Digital circuit InstructionDecoder.dig as structural Verilog
// The InstructionDecoder component, which serves as a hub to control many of the signals to other components. It implements both the fetch operation, and execution of machine code (including decoding).
module InstructionDecoder (
  input  [31:0] Instruction,
  input  Fetch,
  input  Execute,
  input  Clock,
  output [3:0] Reg_dest,
  output [3:0] Reg_B,
  output [3:0] Reg_A,
  output [2:0] Opcode,
  output [31:0] Constant,
  output [2:0] Format,
  output f,
  output [3:0] Condition
);

  wire and_2_out, ARITH2_3_lt, check_halt_write_lt, feedback_loop_q, is_it_1_eq, not_1_out, plus_1_s;
  wire [31:0] and_1_out, c10toc32_1_c32, multiplexer_1_out, multiplexer_2_out;
  wire [31:4] IR_q;

  not not_1 (not_1_out, is_it_1_eq);
  Register #(.Bits(32)) IR (.D(Instruction), .C(Clock), .en(Fetch), .Q({IR_q, Condition}));
  Register feedback_loop (.D(plus_1_s), .C(Clock), .en(not_1_out), .Q(feedback_loop_q));
  Comparator is_it_1 (.a(feedback_loop_q), .b(1'b1), .eq(is_it_1_eq));  // open: gt, lt
  Add plus_1 (.a(1'b1), .b(feedback_loop_q), .c_i(1'b0), .s(plus_1_s));  // open: c_o
  Multiplexer #(.Bits(32)) multiplexer_1 (.sel(Execute), .in_0({32{1'b0}}), .in_1({32{1'b1}}), .out(multiplexer_1_out));
  assign and_1_out = {IR_q, Condition} & multiplexer_1_out;  // And and_1, 32 bits wide
  and and_2 (and_2_out, Fetch, is_it_1_eq);
  Multiplexer #(.Bits(32)) multiplexer_2 (
    .sel(and_2_out), .in_0(and_1_out), .in_1(32'h60040ff0), .out(multiplexer_2_out));
  formatter formatter_1 (.Instruction(multiplexer_2_out), .format(Format));
  c10toc32 c10toc32_1 (.c10(multiplexer_2_out[25:16]), .c32(c10toc32_1_c32));
  Comparator #(.Bits(3)) check_halt_write (.a(3'b010), .b(Format), .lt(check_halt_write_lt));  // open: gt, eq
  Multiplexer #(.Selector_Bits(3), .Bits(32)) multiplexer_3 (
    .sel(Format), .in_0({32{1'b0}}), .in_1({32{1'b0}}), .in_2(c10toc32_1_c32), .in_3(c10toc32_1_c32),
    .in_4({multiplexer_2_out[29:8], {10{1'b0}}}), .in_5({32{1'b0}}), .in_6(c10toc32_1_c32),
    .in_7({32{1'b0}}), .out(Constant));
  Multiplexer #(.Bits(4)) multiplexer_4 (
    .sel(check_halt_write_lt), .in_0(4'b0000), .in_1(multiplexer_2_out[7:4]), .out(Reg_dest));
  Multiplexer #(.Selector_Bits(3), .Bits(4)) multiplexer_5 (
    .sel(Format), .in_0(4'b0000), .in_1(4'b0000), .in_2(multiplexer_2_out[15:12]), .in_3(4'b0000),
    .in_4(4'b0000), .in_5(multiplexer_2_out[15:12]), .in_6(4'b0000), .in_7(4'b0000), .out(Reg_A));
  Multiplexer #(.Selector_Bits(3), .Bits(4)) multiplexer_6 (
    .sel(Format), .in_0(4'b0000), .in_1(4'b0000), .in_2(multiplexer_2_out[11:8]),
    .in_3(multiplexer_2_out[11:8]), .in_4(Reg_dest), .in_5(multiplexer_2_out[11:8]),
    .in_6(multiplexer_2_out[11:8]), .in_7(4'b0000), .out(Reg_B));
  Comparator #(.Bits(3)) ARITH2_3 (.a(3'b100), .b(Format), .lt(ARITH2_3_lt));  // open: gt, eq
  Multiplexer #(.Bits(3)) multiplexer_7 (
    .sel(ARITH2_3_lt), .in_0(3'b110), .in_1(multiplexer_2_out[30:28]), .out(Opcode));
  Multiplexer multiplexer_8 (.sel(ARITH2_3_lt), .in_0(1'b0), .in_1(multiplexer_2_out[27]), .out(f));

  // Notes on the sheet:
  //   Instruction: The instruction machine code input. If the CPU is in the fetch phase and a rising clock signal occurs, this machine code is stored in the internal instruction register (IR), so that it can be decoded and executed.
  //   Reg_dest: Destination register output, which determines the register that should store the result of a data operation. A data operation is either an ALU computation, or a read from an external device, such as RAM.
  //   Reg_B: A register output, which determines the register to be used for the first operand.
  //   Reg_A: A register output, which determines the register to be used for the first operand.
  //   Opcode: Opcode output, which determines the operation the ALU should perform.
  //   Constant: right padded c22 or sign extended c10
  //   Format: Format output, determines what kind of machine code is given
  //   f: Set flags y/n
  //   Condition: Instruction condition output, which contains the condition under which the instruction should be executed.
  //   This prevents the PC starting at 4
  //   cond
  //   flag
  //   Opcode
  //   B
  //   A
  //   c10
  //   c22
  //   D
  //   RegB also becomes
  //   RegD whenever we 
  //   are performing a LOADHI
  //   default opcode is 110
  //   needed for LOADHI, WRITE, READ
endmodule
