// Digital circuit Timer.dig as structural Verilog
// The Timer component that contains a FSM which determines the current CPU phase and state. Once the processor starts, it will initialize to the fetch phase.
// The state is encoded as a 3-bit value: 0=Fetch, 1=Test, 2=Execute, 3=Pause, 4=Halted, 5+6+7=Unused.
module Timer (
  input  Clock,
  input  TestSucceeds,
  input  Halt,
  output Halted,
  output Fetch,
  output Execute
);

  wire delay_1_out, F_out, or_1_out, xor_1_out;
  wire [2:0] PHASE_q, timertransitions_1_phase_2;

  Delay delay_1 (.in(Clock), .out(delay_1_out));
  xor xor_1 (xor_1_out, Clock, delay_1_out);
  D_FF #(.Bits(3)) PHASE (.D(timertransitions_1_phase_2), .C(xor_1_out), .Q(PHASE_q));  // open: nQ
  or or_1 (or_1_out, TestSucceeds, F_out);
  Button F (.out(F_out));
  Decoder #(.Selector_Bits(3)) decoder_1 (
    .sel(PHASE_q), .out_0(Fetch), .out_2(Execute), .out_4(Halted));  // open: out_1, out_3, out_5, out_6, out_7
  TimerTransitions timertransitions_1 (
    .Phase(PHASE_q), .TestSucceeds(or_1_out), .Halt(Halt), .Phase_2(timertransitions_1_phase_2));

  // Notes on the sheet:
  //   TestSucceeds: Test succeeded input pin that determines if the fetched instruction should be executed. If high during the test phase, the CPU will move to the execute phase, otherwise it returns to the fetch phase.
  //   Halt: If this input pin is high -and the CPU enters the execute phase- the CPU will enter the halted state.
  //   Halted: Determines if the CPU is currently in the halted state.
  //   Fetch: Determines if the CPU is currently in the fetch phase.
  //   Execute: Determines if the CPU is currently in the execute phase.
  //   DetectEdge
endmodule

/* Test case BadHalt:
Clock TestSucceeds Halt Fetch Execute Halted

# check if at fetch if an incorrect halt value was provided
0     0            1    1     0       0
*/

/* Test case BadHaltTS:
Clock TestSucceeds Halt Fetch Execute Halted

# check if at fetch if incorrect halt and test succeeds values were provided
0     1            1    1     0       0
*/

/* Test case BadTS:
Clock TestSucceeds Halt Fetch Execute Halted

# check if at fetch if an incorrect test succeeds value was provided
0     1            0    1     0       0
*/

/* Test case:
Clock TestSucceeds Halt Fetch Execute Halted

# check if at fetch
0     0            0    1     0       0

# test failed, check if remains at fetch
C     0            0    1     0       0

# test passed, check if at execute
C     1            0    0     1       0

# check if back to fetch
C     1            0    1     0       0

# halt
C     0            1    1     0       0
C     1            1    0     1       0
C     1            1    0     0       1

# check if stays halted
C     0            0    0     0       1
C     1            0    0     0       1
C     0            0    0     0       1
*/
