// Digital circuit c10toc32.dig as structural Verilog
module c10toc32 (
  input  [9:0] c10,
  output [31:0] c32
);

  Multiplexer #(.Bits(22)) multiplexer_1 (.sel(c10[9]), .in_0({22{1'b0}}), .in_1({22{1'b1}}), .out(c32[31:10]));

  assign c32[9:0] = c10;
endmodule
