// Digital circuit formatter.dig as structural Verilog
module formatter (
  input  [31:0] Instruction,
  output [2:0] format
);

  wire _4_7__eq__0000_eq, _12_15__eq__0000_2_eq, _12_15__eq__0000_eq, _16_25__eq__0_eq, and_1_out, and_2_out,
       and_3_out, and_4_out, and_5_out, and_6_out, and_7_out, and_8_out, and_9_out, and_10_out, and_11_out,
       comparator_1_eq;
  wire [27:0] not_1_out;

  and and_1 (and_1_out, Instruction[31], Instruction[30]);
  and and_2 (and_2_out, Instruction[31], ~Instruction[30]);  // And
  and and_3 (and_3_out, ~Instruction[31], Instruction[26]);  // And
  and and_4 (and_4_out, ~Instruction[31], ~Instruction[26]);  // And
  assign not_1_out = ~{28{1'b0}};  // Not not_1, 28 bits wide
  Comparator #(.Bits(28)) comparator_1 (.a(not_1_out), .b(Instruction[31:4]), .eq(comparator_1_eq));  // open: gt, lt
  and and_5 (and_5_out, ~Instruction[26], ~Instruction[27], ~Instruction[28], Instruction[29], and_1_out);  // And
  and and_6 (and_6_out, ~Instruction[26], ~Instruction[27], ~Instruction[28], ~Instruction[29], and_1_out);  // And
  Comparator #(.Bits(4)) _4_7__eq__0000 (.a(4'b0000), .b(Instruction[7:4]), .eq(_4_7__eq__0000_eq));  // open: gt, lt
  Comparator #(.Bits(4)) _12_15__eq__0000 (
    .a(4'b0000), .b(Instruction[15:12]), .eq(_12_15__eq__0000_eq));  // open: gt, lt
  Comparator #(.Bits(10)) _16_25__eq__0 (
    .a({10{1'b0}}), .b(Instruction[25:16]), .eq(_16_25__eq__0_eq));  // open: gt, lt
  Comparator #(.Bits(4)) _12_15__eq__0000_2 (
    .a(4'b0000), .b(Instruction[15:12]), .eq(_12_15__eq__0000_2_eq));  // open: gt, lt
  and and_7 (and_7_out, _16_25__eq__0_eq, and_3_out);
  and and_8 (and_8_out, _12_15__eq__0000_2_eq, and_4_out);
  and and_9 (and_9_out, _4_7__eq__0000_eq, and_5_out);
  and and_10 (and_10_out, _12_15__eq__0000_eq, and_6_out);
  and and_11 (and_11_out, ~comparator_1_eq, ~and_9_out, ~and_10_out, ~and_2_out, ~and_7_out, ~and_8_out);  // And
  PriorityEncoder #(.Selector_Bits(3)) priorityencoder_1 (
    .in0(and_11_out), .in1(comparator_1_eq), .in2(and_9_out), .in3(and_10_out), .in4(and_2_out),
    .in5(and_7_out), .in6(and_8_out), .in7(1'b0), .num(format));  // open: any

  // Notes on the sheet:
  //   11
  //   10
  //   0 _ _ _ _ 1
  //   0 _ _ _ _ 0
  //   111000
  //   110000
  //   case 1
  //   case 2
  //   case 3
  //   case 4
  //   case 5
  //   case 6
  //   if none of the 6 cases 
  //   is true, it is invalid
  //   case 0
  //   invalid
  //   filler bit
endmodule
